# Fritzing sketch DHT11 (saved by Fritzing 0.9.2b)
circuit board: 8.46667cm x 5.64444cm

parts:
  Part1 = Arduino Ethernet Shield (Rev3)
  DHT1 = DHT11 Humitidy and Temperature Sensor

nets:
  N1: Part1.PWM_D9, DHT1.DATA
  5V: Part1.5V, DHT1.VDD
  GND: Part1.GND, DHT1.GND

custom parts:
  DHT11 Humitidy and Temperature Sensor: DHT11 Humidity and Temperature Sensor
