# Fritzing sketch display_time (saved by Fritzing 0.9.2b)
breadboards: 1

parts:
  Part1 = Arduino Ethernet Shield (Rev3)
  U1 = LCD-16X2 [package=lcd-16x2]
  R1 = Rotary Potentiometer (Large) [maximum_resistance=100kΩ package=THT]
  R2 = Resistor [tolerance=±5% resistance=220 package="0805 [SMD]"]

nets (from the breadboard view):
  5V: Part1.5V, U1.VDD, U1.R_W, R1.leg1, R2.Pin_0
  N1: Part1.D8, U1.E
  N2: Part1.PWM_D9, U1.RS
  N3: Part1.D2, U1.DB7
  N4: Part1.PWM_D3, U1.DB6
  N5: Part1.SDCS, U1.DB5
  N6: Part1.PWM_D5, U1.DB4
  GND: Part1.GND, U1.VSS, U1.K, R1.leg2
  N7: U1.VO, R1.wiper
  N8: U1.A, R2.Pin_1
