# Fritzing sketch ethernet_shield_connection (saved by Fritzing 0.9.2b)

parts:
  Part1 = Arduino Uno (Rev3)
  Part2 = Arduino Ethernet Shield (Rev3)

nets:
  N1: Part1.D10_PWM/SS, Part2.ETH_CS
  N2: Part1.D11_PWM/MOSI, Part2.PWM_D11
  N3: Part1.D12/MISO, Part2.SPI/D12
  N4: Part1.D13/SCK, Part2.SPI/D13
